# Fritzing sketch SmartRoomController (saved by Fritzing 1.0.0rc)
breadboards: 1

parts:
  A1 = Particle - Photon2
  OLED_I2C1 = OLED 128x64 I2C Monochrome Display
  OLED_I2C2 = OLED 128x64 I2C Monochrome Display
  J1 = Basic Servo
  J2 = Basic Servo
  Part1 = 12 NeoPixel Ring [part_number=1643]
  U1 = ENCODER_RGB [package=encoder_led_2]
  Mod1 = Passive Buzzer

nets:
  VCC: A1.Pin_2, A1.Pin_31, OLED_I2C2.VDD, J1.vcc, J2.vcc, U1.+, Mod1.-
  GND: A1.Pin_4, A1.Pin_32, OLED_I2C1.GND, OLED_I2C2.GND, J1.gnd, J2.gnd, U1.C, Mod1.NC
  N1: A1.Pin_7, J1.pulse
  N2: A1.Pin_8, J2.pulse
  N3: A1.Pin_10, U1.R
  N4: A1.Pin_11, U1.G
  N5: A1.Pin_12, U1.SW
  N6: A1.Pin_13, Mod1.S
  N7: A1.Pin_14, U1.B#2
  N8: A1.Pin_15, U1.A
  N9: A1.Pin_17, OLED_I2C1.SDA, OLED_I2C2.SDA
  N10: A1.Pin_18, OLED_I2C1.SCK, OLED_I2C2.SCK
  N11: A1.Pin_19, Part1.IN
  N12: A1.Pin_22, U1.B#8
  N13: A1.Pin_26, Part1.VDD

custom parts:
  Particle - Photon2: The Photon 2 is a microcontroller and Wi-Fi networking developed by particle. Features: 802.11a/b/g/n Wi-Fi, 2.4 GHz and 5 GHz Integrated PCB antenna Integrated U.FL connector for external antenna Integrated RF switch BLE 5 using same antenna as Wi-Fi Realtek RTL8721DM MCU ARM Cortex M33 CPU, 200 MHz 2048 KB (2 MB) user application maximum size 3072 KB (3 MB) of RAM available to user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
  12 NeoPixel Ring: 12 ultra bright smart LED NeoPixels are arranged in a circle with 1.5" (37mm) outer diameter. The rings are 'chainable' - connect the output pin of one to the input pin of another. Use only one microcontroller pin to control as many as you can chain together! Each LED is addressable as the driver chip is inside the LED. Each one has ~18mA constant current drive so the color will be very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
  ENCODER_RGB: SparkFun RGB rotary Encoder
